// Logisim project Questão 2 - Multiplexador.circ as structural Verilog: 1 circuit, main circuit main
module main (
  input  [1:0] SELETOR,
  input  INPUT,
  output S1,
  output S2,
  output S3,
  output S4
);

  wire _00_out, _01_out, _10_out, _11_out, not_1_out, not_2_out, not_3_out, not_4_out;

  not not_1 (not_1_out, SELETOR[1]);
  not not_2 (not_2_out, SELETOR[0]);
  not not_3 (not_3_out, SELETOR[1]);
  not not_4 (not_4_out, SELETOR[0]);
  and _00 (_00_out, not_1_out, not_2_out);
  and _01 (_01_out, not_3_out, SELETOR[0]);
  and _10 (_10_out, SELETOR[1], not_4_out);
  and _11 (_11_out, SELETOR[0], SELETOR[1]);
  and and_1 (S1, INPUT, _00_out);
  and and_2 (S2, INPUT, _01_out);
  and and_3 (S3, INPUT, _10_out);
  and and_4 (S4, INPUT, _11_out);
endmodule
